# Fritzing sketch TalkingPlant (saved by Fritzing 0.9.3b)
breadboards: 1

parts:
  WeMos_D1_Mini1 = WeMos D1 Mini
  U1 = 2-Channel 5v Relay Shield [package=relay-2ch5v10a]
  Componente2 = BME280 Breakout
  Componente3 = Soil Moisture Sensor
  Componente4 = 16 NeoPixel Ring [part_number=1463]
  LM1 = RioRand LM2596

nets:
  3V3: WeMos_D1_Mini1.3V3, Componente2.3.3V, Componente3.VCC
  N1: WeMos_D1_Mini1.A0, Componente3.SIG
  N2: WeMos_D1_Mini1.D1, Componente2.SDI/SDA
  N3: WeMos_D1_Mini1.D2, Componente2.SCK/SCL
  N4: WeMos_D1_Mini1.D3, Componente4.IN
  N5: WeMos_D1_Mini1.D5, U1.IN2
  N6: WeMos_D1_Mini1.D6, U1.IN1
  GND: WeMos_D1_Mini1.G, Componente2.GND, Componente3.GND
  N7: Componente4.GND, LM1.Pin_3
  N8: Componente4.VDD, LM1.Pin_2

custom parts:
  WeMos D1 Mini: The D1 mini is a mini wifi board based on ESP-8266EX.
  2-Channel 5v Relay Shield: 2 Channel 5v Relay Shield w. 2x SPD-06VDC-SD-C
  16 NeoPixel Ring: 16 ultra bright smart LED NeoPixels are arranged in a circle with 1.75" (44.5mm) outer diameter. The rings are 'chainable' - connect the output pin of one to the input pin of another. Use only one microcontroller pin to control as many as you can chain together! Each LED is addressable as the driver chip is inside the LED. Each one has ~18mA constant current drive so the color will be very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
